// Logisim project Circuitos.circ as structural Verilog: 9 circuits, main circuit ADD
module ADD (
  input  A,
  input  B,
  input  Vai,
  output out_4,
  output out_5
);

  wire and_1_out, and_2_out, or_1_out, xor_1_out;

  xor xor_1 (xor_1_out, B, Vai);
  or or_1 (or_1_out, B, Vai);
  and and_1 (and_1_out, B, Vai);
  xor xor_2 (out_4, xor_1_out, A);
  and and_2 (and_2_out, or_1_out, A);
  or or_2 (out_5, and_2_out, and_1_out);
endmodule

module ADD4 (
  input  [3:0] in_1,
  input  [3:0] in_2,
  output out_3,
  output [3:0] out_4
);

  wire add_2_out_5, add_3_out_5, add_4_out_5;

  ADD add_1 (.out_4(out_4[3]), .out_5(out_3), .A(in_2[3]), .B(in_1[3]), .Vai(add_2_out_5));
  ADD add_2 (.out_4(out_4[2]), .out_5(add_2_out_5), .A(in_2[2]), .B(in_1[2]), .Vai(add_4_out_5));
  ADD add_3 (.out_4(out_4[0]), .out_5(add_3_out_5), .A(in_2[0]), .B(in_1[0]), .Vai(1'b0));
  ADD add_4 (.out_4(out_4[1]), .out_5(add_4_out_5), .A(in_2[1]), .B(in_1[1]), .Vai(add_3_out_5));
endmodule

module RotD (
  input  [3:0] in_1,
  input  [1:0] in_2,
  output [3:0] out_3
);

  wire and_1_out, and_2_out, and_3_out, and_4_out, and_5_out, and_6_out, and_7_out, and_8_out, and_9_out;

  and and_1 (and_1_out, in_1[0], ~in_2[1], ~in_2[0]);  // AND_Gate
  and and_2 (and_2_out, in_1[1], ~in_2[1], in_2[0]);  // AND_Gate
  and and_3 (and_3_out, in_1[2], in_2[1], ~in_2[0]);  // AND_Gate
  and and_4 (and_4_out, in_1[3], in_2[1], in_2[0]);
  and and_5 (and_5_out, in_1[1], ~in_2[1], ~in_2[0]);  // AND_Gate
  and and_6 (and_6_out, in_1[2], ~in_2[1], in_2[0]);  // AND_Gate
  and and_7 (and_7_out, in_1[3], in_2[1], ~in_2[0]);  // AND_Gate
  and and_8 (and_8_out, in_1[2], ~in_2[1], ~in_2[0]);  // AND_Gate
  and and_9 (and_9_out, in_1[3], ~in_2[1], in_2[0]);  // AND_Gate
  and and_10 (out_3[3], in_1[3], ~in_2[1], ~in_2[0]);  // AND_Gate
  or or_1 (out_3[0], and_1_out, and_2_out, and_3_out, and_4_out);
  or or_2 (out_3[1], and_5_out, and_6_out, and_7_out);
  or or_3 (out_3[2], and_8_out, and_9_out);
endmodule

module RotE (
  input  [3:0] in_1,
  input  [1:0] in_2,
  output [3:0] out_3
);

  wire and_1_out, and_2_out, and_3_out, and_4_out, and_5_out, and_6_out, and_7_out, and_8_out, and_9_out;

  and and_1 (and_1_out, in_1[3], ~in_2[1], ~in_2[0]);  // AND_Gate
  and and_2 (and_2_out, in_1[2], ~in_2[1], in_2[0]);  // AND_Gate
  and and_3 (and_3_out, in_1[1], in_2[1], ~in_2[0]);  // AND_Gate
  and and_4 (and_4_out, in_1[0], in_2[1], in_2[0]);
  and and_5 (and_5_out, in_1[2], ~in_2[1], ~in_2[0]);  // AND_Gate
  and and_6 (and_6_out, in_1[1], ~in_2[1], in_2[0]);  // AND_Gate
  and and_7 (and_7_out, in_1[0], in_2[1], ~in_2[0]);  // AND_Gate
  and and_8 (and_8_out, in_1[1], ~in_2[1], ~in_2[0]);  // AND_Gate
  and and_9 (and_9_out, in_1[0], ~in_2[1], in_2[0]);  // AND_Gate
  and and_10 (out_3[0], in_1[0], ~in_2[1], ~in_2[0]);  // AND_Gate
  or or_1 (out_3[3], and_1_out, and_2_out, and_3_out, and_4_out);
  or or_2 (out_3[2], and_5_out, and_6_out, and_7_out);
  or or_3 (out_3[1], and_8_out, and_9_out);
  RotD rotd_1 ();  // open: in_1, in_2, out_3
endmodule

module Main (
);

  ADD4 add4_1 ();  // open: in_2, out_3, in_1, out_4
  DEC dec_1 ();  // open: D0, D1, D2, D3, D4, D5, D6, D7, ABC
  SUB4 sub4_1 ();  // open: in_2, out_3, in_1, out_4
  RotE rote_1 ();  // open: in_1, in_2, out_3
  RotD rotd_1 ();  // open: in_1, in_2, out_3
endmodule

module SUB4 (
  input  [3:0] in_1,
  input  [3:0] in_2,
  output out_3,
  output [3:0] out_4
);

  wire sub_2_out_5, sub_3_out_5, sub_4_out_5;

  SUB sub_1 (.out_4(out_4[3]), .out_5(out_3), .A(in_2[3]), .B(in_1[3]), .Vai(sub_2_out_5));
  SUB sub_2 (.out_4(out_4[2]), .out_5(sub_2_out_5), .A(in_2[2]), .B(in_1[2]), .Vai(sub_4_out_5));
  SUB sub_3 (.out_4(out_4[0]), .out_5(sub_3_out_5), .A(in_2[0]), .B(in_1[0]), .Vai(1'b0));
  SUB sub_4 (.out_4(out_4[1]), .out_5(sub_4_out_5), .A(in_2[1]), .B(in_1[1]), .Vai(sub_3_out_5));
endmodule

module SUB (
  input  A,
  input  B,
  input  Vai,
  output out_4,
  output out_5
);

  wire and_1_out, and_2_out, or_1_out, xor_1_out;

  xor xor_1 (xor_1_out, B, Vai);
  or or_1 (or_1_out, B, Vai);
  and and_1 (and_1_out, B, Vai);
  xor xor_2 (out_4, xor_1_out, A);
  and and_2 (and_2_out, or_1_out, ~A);  // AND_Gate
  or or_2 (out_5, and_2_out, and_1_out);
endmodule

module DEC (
  input  [2:0] ABC,
  output D0,
  output D1,
  output D2,
  output D3,
  output D4,
  output D5,
  output D6,
  output D7
);

  wire not_1_out, not_2_out, not_3_out, not_4_out, not_5_out, not_6_out, not_7_out, not_8_out, not_9_out,
       not_10_out, not_11_out, not_12_out;

  not not_1 (not_1_out, ABC[2]);
  not not_2 (not_2_out, ABC[2]);
  not not_3 (not_3_out, ABC[2]);
  not not_4 (not_4_out, ABC[2]);
  not not_5 (not_5_out, ABC[2]);
  not not_6 (not_6_out, ABC[2]);
  not not_7 (not_7_out, ABC[2]);
  not not_8 (not_8_out, ABC[2]);
  not not_9 (not_9_out, ABC[2]);
  not not_10 (not_10_out, ABC[2]);
  not not_11 (not_11_out, ABC[2]);
  not not_12 (not_12_out, ABC[2]);
  and and_1 (D7, ABC[2], ABC[2], ABC[2]);
  and and_2 (D0, not_1_out, not_2_out, not_3_out);
  and and_3 (D1, not_4_out, not_5_out, ABC[2]);
  and and_4 (D2, not_6_out, ABC[2], not_7_out);
  and and_5 (D3, not_8_out, ABC[2], ABC[2]);
  and and_6 (D4, ABC[2], not_9_out, not_10_out);
  and and_7 (D5, ABC[2], not_11_out, ABC[2]);
  and and_8 (D6, ABC[2], ABC[2], not_12_out);

  assign ABC[1:0] = {2{ABC[2]}};
endmodule

module BUFFER (
  input  [3:0] in_1,
  input  in_2,
  output [3:0] out_3
);

  assign out_3[2] = in_2 ? in_1[2] : 1'bz;  // Controlled_Buffer controlled_buffer_1
  assign out_3[3] = in_2 ? in_1[3] : 1'bz;  // Controlled_Buffer controlled_buffer_2
  assign out_3[1] = in_2 ? in_1[1] : 1'bz;  // Controlled_Buffer controlled_buffer_3
  assign out_3[0] = in_2 ? in_1[0] : 1'bz;  // Controlled_Buffer controlled_buffer_4
endmodule
